// Logisim project cpu.circ as structural Verilog: 1 circuit, main circuit main
module main (
);

  wire and_2_out, and_3_out, and_4_out, button_1_out, clock_1_out, demultiplexer_1_out0,
       demultiplexer_1_out1, demultiplexer_1_out2, demultiplexer_1_out3, multiplexer_2_out, nor_1_out,
       not_1_out, not_2_out, not_4_out, or_2_out;
  wire [1:0] multiplexer_1_out, multiplexer_3_out, rom_1_data_2;
  wire [2:0] rom_1_data_3;
  wire [3:0] multiplexer_4_out, multiplexer_5_out, multiplexer_7_out;
  wire [6:0] multiplexer_9_out;
  wire [7:0] adder_1_out, adder_2_out, and_1_out, multiplexer_8_out, multiplexer_10_out, not_3_out, or_1_out,
       register_1_q, register_2_q, register_3_q, register_4_q, register_5_q, xor_1_out;
  wire [7:2] rom_1_data;
  wire [7:7] multiplexer_9_out_2;
  wire [8:1] multiplexer_6_out;
  wire [9:0] shifter_1_out, shifter_2_out;

  ROM rom_1 (.addr(register_1_q), .data({rom_1_data[7], rom_1_data_3, rom_1_data[3:2], rom_1_data_2}));
  Clock clock_1 (.out(clock_1_out));
  LED led_1 (.in(clock_1_out));
  Register register_1 (.D(adder_1_out), .en(1'b1), .clk(clock_1_out), .Q(register_1_q), .clr(button_1_out));
  Button button_1 (.out(button_1_out));
  // Probe on {rom_1_data[7], rom_1_data_3, rom_1_data[3:2], rom_1_data_2}
  Adder adder_1 (.a(register_1_q), .b(8'h1), .out(adder_1_out), .cin(1'b0));  // open: cout
  // Probe on multiplexer_1_out
  Multiplexer #(.width(2), .enable("false")) multiplexer_1 (
    .in0(rom_1_data[3:2]), .in1(rom_1_data_3[1:0]), .out(multiplexer_1_out), .sel(not_1_out));
  // Probe on not_1_out
  not not_1 (not_1_out, rom_1_data[7]);
  Register register_2 (
    .D(multiplexer_8_out), .en(demultiplexer_1_out0), .clk(clock_1_out), .Q(register_2_q), .clr(button_1_out));
  Demultiplexer #(.select(2), .enable("false")) demultiplexer_1 (
    .out0(demultiplexer_1_out0), .out1(demultiplexer_1_out1), .out2(demultiplexer_1_out2),
    .out3(demultiplexer_1_out3), .in(multiplexer_2_out), .sel(multiplexer_1_out));
  // Probe on multiplexer_2_out
  Multiplexer #(.enable("false")) multiplexer_2 (.in0(1'b1), .in1(and_2_out), .out(multiplexer_2_out), .sel(not_2_out));
  not not_2 (not_2_out, not_1_out);
  Multiplexer #(.width(2), .enable("false")) multiplexer_3 (
    .in0(rom_1_data[3:2]), .in1(rom_1_data_3[1:0]), .out(multiplexer_3_out), .sel(not_1_out));
  // Probe on not_1_out
  Multiplexer #(.width(4), .enable("false")) multiplexer_4 (
    .in0(multiplexer_6_out[8:5]), .in1(multiplexer_6_out[4:1]), .out(multiplexer_4_out), .sel(rom_1_data_3[2]));
  Register register_3 (
    .D(multiplexer_8_out), .en(demultiplexer_1_out1), .clk(clock_1_out), .Q(register_3_q), .clr(button_1_out));
  // Probe on multiplexer_3_out
  Multiplexer #(.width(4), .enable("false")) multiplexer_5 (
    .in0({rom_1_data[3:2], rom_1_data_2}), .in1(multiplexer_4_out), .out(multiplexer_5_out),
    .sel(rom_1_data_3[2]));
  Register register_4 (
    .D(multiplexer_8_out), .en(demultiplexer_1_out2), .clk(clock_1_out), .Q(register_4_q), .clr(button_1_out));
  Multiplexer #(.select(2), .width(8), .enable("false")) multiplexer_6 (
    .in0(register_2_q), .in1(register_3_q), .in2(register_4_q), .in3(register_5_q), .out(multiplexer_6_out),
    .sel(multiplexer_3_out));
  // Probe on multiplexer_6_out
  Multiplexer #(.width(4), .enable("false")) multiplexer_7 (
    .in0(multiplexer_4_out), .in1({rom_1_data[3:2], rom_1_data_2}), .out(multiplexer_7_out),
    .sel(rom_1_data_3[2]));
  // Probe on multiplexer_8_out
  Multiplexer #(.width(8), .enable("false")) multiplexer_8 (
    .in0(multiplexer_10_out), .in1({multiplexer_7_out, multiplexer_5_out}), .out(multiplexer_8_out),
    .sel(not_1_out));
  Register register_5 (
    .D(multiplexer_8_out), .en(demultiplexer_1_out3), .clk(clock_1_out), .Q(register_5_q), .clr(button_1_out));
  TTY tty_1 (.data(multiplexer_9_out), .clk(clock_1_out), .we(and_3_out), .clr(and_4_out));
  assign not_3_out = ~multiplexer_6_out;  // NOT_Gate not_3, 8 bits wide
  assign or_1_out = {multiplexer_9_out_2[7], multiplexer_9_out} | multiplexer_6_out;  // OR_Gate or_1, 8 bits wide
  assign and_1_out = {multiplexer_9_out_2[7], multiplexer_9_out} & multiplexer_6_out;  // AND_Gate and_1, 8 bits wide
  assign xor_1_out = {multiplexer_9_out_2[7], multiplexer_9_out} ^ multiplexer_6_out;  // XOR_Gate xor_1, 8 bits wide
  or or_2 (or_2_out, rom_1_data_3[0], rom_1_data_3[1], rom_1_data_3[2]);
  Multiplexer #(.select(2), .width(8), .enable("false")) multiplexer_9 (
    .in0(register_2_q), .in1(register_3_q), .in2(register_4_q), .in3(register_5_q),
    .out({multiplexer_9_out_2[7], multiplexer_9_out}), .sel(rom_1_data_2));
  // Probe on {multiplexer_9_out_2[7], multiplexer_9_out}
  Adder adder_2 (
    .a({multiplexer_9_out_2[7], multiplexer_9_out}), .b(multiplexer_6_out), .out(adder_2_out), .cin(1'b0));  // open: cout
  not not_4 (not_4_out, or_2_out);
  and and_2 (and_2_out, or_2_out, rom_1_data[7]);
  nor nor_1 (nor_1_out, rom_1_data_2[0], rom_1_data_2[1]);
  and and_3 (and_3_out, not_4_out, rom_1_data[7], nor_1_out);
  and and_4 (and_4_out, multiplexer_9_out_2[7], and_3_out);
  Shifter #(.width(10)) shifter_1 (
    .in({1'b0, multiplexer_6_out, 1'b0}), .\dist (multiplexer_9_out[3:0]), .out(shifter_1_out));
  Shifter #(.width(10), .shift("lr")) shifter_2 (
    .in({1'b0, multiplexer_6_out, 1'b0}), .\dist (multiplexer_9_out[3:0]), .out(shifter_2_out));
  Multiplexer #(.select(3), .width(8), .enable("false")) multiplexer_10 (
    .in0({8{1'b0}}), .in1(or_1_out), .in2(and_1_out), .in3(xor_1_out), .in4(adder_2_out),
    .in5(shifter_1_out[8:1]), .in6(shifter_2_out[8:1]), .in7(not_3_out), .out(multiplexer_10_out),
    .sel(rom_1_data_3));
  // Probe on multiplexer_10_out

  // Notes on the sheet:
  //   contents of rom_1 (hex, n*v repeats v):
  //   6 4e f0 13 50 d1 22 61 c8 32 70 eb 6 4e b2 96 a4 c4 c1
  //   RESET
  //   PC
  //   WRITE SELECT
  //   R0
  //   R1
  //   REG OUT A
  //   HI
  //   LO
  //   R2
  //   HI
  //   REG IN
  //   LO
  //   R3
  //   REG OUT B
endmodule
